// Logisim project ALU - 8 BIT.circ as structural Verilog: 9 circuits, main circuit main
module main (
  input  [7:0] A,
  input  [7:0] B,
  input  Cin,
  input  [2:0] Bit_Selector,
  output \A_é_maior ,
  output Iguais,
  output Zero,
  output [7:0] Output,
  output Cout
);

  ALU alu_1 (
    .A(A), .B(B), .Cin(Cin), .Bit_Selector(Bit_Selector), .\A_é_maior (\A_é_maior ), .Iguais(Iguais),
    .Zero(Zero), .Output(Output), .Cout(Cout));

  // Notes on the sheet:
  //   000 - ADD
  //   001 - SHR
  //   010 - SHL
  //   011 - SUB
  //   100 - AND
  //   101 - OR
  //   110 - XOR
  //   111 - Nada
endmodule

module Registrador (
  input  Load,
  input  Load_2,
  input  [7:0] Entrada,
  output [7:0] \Saída 
);

  wire and_1_out, and_2_out, and_3_out, and_4_out, and_5_out, and_6_out, and_7_out, and_8_out, and_9_out,
       and_10_out, and_11_out, and_12_out, and_13_out, and_14_out, and_15_out, and_16_out, clock_1_out,
       d_ff_1_q, d_ff_2_q, d_ff_3_q, d_ff_4_q, d_ff_5_q, d_ff_6_q, d_ff_7_q, d_ff_8_q, not_1_out, not_2_out,
       not_3_out, not_4_out, not_5_out, not_6_out, not_7_out, not_8_out, or_1_out, or_2_out, or_3_out,
       or_4_out, or_5_out, or_6_out, or_7_out, or_8_out;

  not not_1 (not_1_out, Load_2);
  not not_2 (not_2_out, Load_2);
  not not_3 (not_3_out, Load_2);
  not not_4 (not_4_out, Load_2);
  not not_5 (not_5_out, Load_2);
  not not_6 (not_6_out, Load_2);
  not not_7 (not_7_out, Load_2);
  not not_8 (not_8_out, Load_2);
  and and_1 (and_1_out, not_1_out, d_ff_1_q);
  and and_2 (and_2_out, Load_2, Entrada[0]);
  and and_3 (and_3_out, not_2_out, d_ff_2_q);
  and and_4 (and_4_out, Load_2, Entrada[1]);
  and and_5 (and_5_out, not_3_out, d_ff_3_q);
  and and_6 (and_6_out, Load_2, Entrada[2]);
  and and_7 (and_7_out, not_4_out, d_ff_4_q);
  and and_8 (and_8_out, Load_2, Entrada[3]);
  and and_9 (and_9_out, not_5_out, d_ff_5_q);
  and and_10 (and_10_out, Load_2, Entrada[4]);
  and and_11 (and_11_out, not_6_out, d_ff_6_q);
  and and_12 (and_12_out, Load_2, Entrada[5]);
  and and_13 (and_13_out, not_7_out, d_ff_7_q);
  and and_14 (and_14_out, Load_2, Entrada[6]);
  and and_15 (and_15_out, not_8_out, d_ff_8_q);
  and and_16 (and_16_out, Load_2, Entrada[7]);
  or or_1 (or_1_out, and_1_out, and_2_out);
  or or_2 (or_2_out, and_3_out, and_4_out);
  or or_3 (or_3_out, and_5_out, and_6_out);
  or or_4 (or_4_out, and_7_out, and_8_out);
  or or_5 (or_5_out, and_9_out, and_10_out);
  or or_6 (or_6_out, and_11_out, and_12_out);
  or or_7 (or_7_out, and_13_out, and_14_out);
  or or_8 (or_8_out, and_15_out, and_16_out);
  D_Flip_Flop d_ff_1 (.clk(clock_1_out), .D(or_1_out), .Q(d_ff_1_q));  // open: Qn, preset, en, reset
  Clock clock_1 (.out(clock_1_out));
  D_Flip_Flop d_ff_2 (.clk(clock_1_out), .D(or_2_out), .Q(d_ff_2_q));  // open: Qn, preset, en, reset
  D_Flip_Flop d_ff_3 (.clk(clock_1_out), .D(or_3_out), .Q(d_ff_3_q));  // open: Qn, preset, en, reset
  D_Flip_Flop d_ff_4 (.clk(clock_1_out), .D(or_4_out), .Q(d_ff_4_q));  // open: Qn, preset, en, reset
  D_Flip_Flop d_ff_5 (.clk(clock_1_out), .D(or_5_out), .Q(d_ff_5_q));  // open: Qn, preset, en, reset
  D_Flip_Flop d_ff_6 (.clk(clock_1_out), .D(or_6_out), .Q(d_ff_6_q));  // open: Qn, preset, en, reset
  D_Flip_Flop d_ff_7 (.clk(clock_1_out), .D(or_7_out), .Q(d_ff_7_q));  // open: Qn, preset, en, reset
  D_Flip_Flop d_ff_8 (.clk(clock_1_out), .D(or_8_out), .Q(d_ff_8_q));  // open: Qn, preset, en, reset
  and and_17 (\Saída [0], d_ff_1_q, Load);
  and and_18 (\Saída [1], d_ff_2_q, Load);
  and and_19 (\Saída [2], d_ff_3_q, Load);
  and and_20 (\Saída [3], d_ff_4_q, Load);
  and and_21 (\Saída [4], d_ff_5_q, Load);
  and and_22 (\Saída [5], d_ff_6_q, Load);
  and and_23 (\Saída [6], d_ff_7_q, Load);
  and and_24 (\Saída [7], d_ff_8_q, Load);
endmodule

module Left_Shifter (
  input  Carry_in,
  input  [7:0] Entrada,
  output [7:0] \Saída ,
  output Carry_out
);

  wire [6:0] \registrador_1_saída ;

  Registrador registrador_1 (
    .Entrada(Entrada), .\Saída ({Carry_out, \registrador_1_saída }), .Load_2(1'b1), .Load(1'b1));
  Registrador registrador_2 (
    .Entrada({\registrador_1_saída , Carry_in}), .\Saída (\Saída ), .Load_2(1'b1), .Load(1'b1));
endmodule

module Right_Shifter (
  input  [7:0] Entrada,
  input  Shift_In,
  output Shift_Out,
  output [7:0] \Saída 
);

  wire [7:1] \registrador_1_saída ;

  Registrador registrador_1 (
    .Entrada(Entrada), .\Saída ({\registrador_1_saída , Shift_Out}), .Load_2(1'b1), .Load(1'b1));
  Registrador registrador_2 (
    .Entrada({Shift_In, \registrador_1_saída }), .\Saída (\Saída ), .Load_2(1'b1), .Load(1'b1));
endmodule

module Adder (
  input  [7:0] A,
  input  [7:0] B,
  input  Cin,
  output [7:0] Sum,
  output Cout
);

  wire and_1_out, and_2_out, and_3_out, and_4_out, and_5_out, and_6_out, and_7_out, and_8_out, and_9_out,
       and_10_out, and_11_out, and_12_out, and_13_out, and_14_out, and_15_out, and_16_out, or_1_out,
       or_2_out, or_3_out, or_4_out, or_6_out, or_7_out, or_8_out, or_9_out, or_10_out, or_11_out, or_12_out,
       or_13_out, or_14_out, or_15_out, or_16_out, xor_1_out, xor_2_out, xor_3_out, xor_4_out, xor_9_out,
       xor_10_out, xor_11_out, xor_12_out;

  and and_1 (and_1_out, A[7], B[7]);
  or or_1 (or_1_out, B[7], A[7]);
  and and_2 (and_2_out, A[6], B[6]);
  or or_2 (or_2_out, B[6], A[6]);
  xor xor_1 (xor_1_out, A[5], B[5]);
  and and_3 (and_3_out, A[5], B[5]);
  or or_3 (or_3_out, B[5], A[5]);
  xor xor_2 (xor_2_out, A[4], B[4]);
  and and_4 (and_4_out, A[4], B[4]);
  or or_4 (or_4_out, B[4], A[4]);
  xor xor_3 (xor_3_out, A[7], B[7]);
  and and_5 (and_5_out, or_1_out, or_6_out);
  xor xor_4 (xor_4_out, A[6], B[6]);
  and and_6 (and_6_out, or_2_out, or_7_out);
  and and_7 (and_7_out, or_3_out, or_8_out);
  and and_8 (and_8_out, or_4_out, or_13_out);
  xor xor_5 (Sum[7], xor_3_out, or_6_out);
  or or_5 (Cout, and_1_out, and_5_out);
  xor xor_6 (Sum[6], xor_4_out, or_7_out);
  or or_6 (or_6_out, and_2_out, and_6_out);
  xor xor_7 (Sum[5], xor_1_out, or_8_out);
  or or_7 (or_7_out, and_3_out, and_7_out);
  xor xor_8 (Sum[4], xor_2_out, or_13_out);
  or or_8 (or_8_out, and_4_out, and_8_out);
  and and_9 (and_9_out, A[3], B[3]);
  or or_9 (or_9_out, B[3], A[3]);
  and and_10 (and_10_out, A[2], B[2]);
  or or_10 (or_10_out, B[2], A[2]);
  xor xor_9 (xor_9_out, A[1], B[1]);
  and and_11 (and_11_out, A[1], B[1]);
  or or_11 (or_11_out, B[1], A[1]);
  xor xor_10 (xor_10_out, A[0], B[0]);
  and and_12 (and_12_out, A[0], B[0]);
  or or_12 (or_12_out, B[0], A[0]);
  xor xor_11 (xor_11_out, A[3], B[3]);
  and and_13 (and_13_out, or_9_out, or_14_out);
  xor xor_12 (xor_12_out, A[2], B[2]);
  and and_14 (and_14_out, or_10_out, or_15_out);
  and and_15 (and_15_out, or_11_out, or_16_out);
  and and_16 (and_16_out, or_12_out, Cin);
  xor xor_13 (Sum[3], xor_11_out, or_14_out);
  or or_13 (or_13_out, and_9_out, and_13_out);
  xor xor_14 (Sum[2], xor_12_out, or_15_out);
  or or_14 (or_14_out, and_10_out, and_14_out);
  xor xor_15 (Sum[1], xor_9_out, or_16_out);
  or or_15 (or_15_out, and_11_out, and_15_out);
  xor xor_16 (Sum[0], xor_10_out, Cin);
  or or_16 (or_16_out, and_12_out, and_16_out);
endmodule

module _3_to_8 (
  input  A,
  input  B,
  input  C,
  output _000,
  output _001,
  output _010,
  output _011,
  output _100,
  output _101,
  output _110,
  output _111
);

  wire not_1_out, not_2_out, not_3_out;

  not not_1 (not_1_out, A);
  not not_2 (not_2_out, B);
  not not_3 (not_3_out, C);
  and and_1 (_000, not_1_out, not_2_out, not_3_out);
  and and_2 (_001, not_1_out, not_2_out, C);
  and and_3 (_010, not_1_out, not_3_out, B);
  and and_4 (_011, not_1_out, B, C);
  and and_5 (_100, not_2_out, not_3_out, A);
  and and_6 (_101, not_2_out, A, C);
  and and_7 (_110, A, B, not_3_out);
  and and_8 (_111, A, B, C);
endmodule

module Comparator (
  input  [7:0] B,
  input  [7:0] A,
  output Equal,
  output \A__é_Maior ,
  output [7:0] Output
);

  wire and_1_out, and_2_out, and_3_out, and_4_out, and_5_out, and_6_out, and_7_out, and_8_out, and_9_out,
       and_10_out, and_11_out, and_12_out, and_14_out, and_15_out, and_16_out, not_1_out, not_2_out,
       not_3_out, not_4_out, not_5_out, not_6_out, not_7_out, not_8_out, or_1_out, or_2_out, or_3_out,
       or_4_out, or_5_out, or_6_out, or_7_out;

  xor xor_1 (Output[7], A[7], B[7]);
  not not_1 (not_1_out, Output[7]);
  and and_1 (and_1_out, not_1_out, 1'b1);
  xor xor_2 (Output[3], A[3], B[3]);
  not not_2 (not_2_out, Output[3]);
  and and_2 (and_2_out, not_2_out, and_14_out);
  and and_3 (and_3_out, A[7], 1'b1, Output[7]);
  or or_1 (or_1_out, and_3_out, 1'b0);
  and and_4 (and_4_out, A[3], and_14_out, Output[3]);
  or or_2 (or_2_out, and_4_out, or_7_out);
  xor xor_3 (Output[6], A[4], B[4]);
  not not_3 (not_3_out, Output[6]);
  and and_5 (and_5_out, not_3_out, and_1_out);
  xor xor_4 (Output[2], A[2], B[2]);
  not not_4 (not_4_out, Output[2]);
  and and_6 (and_6_out, not_4_out, and_2_out);
  and and_7 (and_7_out, A[4], and_1_out, Output[6]);
  and and_8 (and_8_out, A[2], and_2_out, Output[2]);
  or or_3 (or_3_out, and_7_out, or_1_out);
  or or_4 (or_4_out, and_8_out, or_2_out);
  xor xor_5 (Output[1], A[1], B[1]);
  xor xor_6 (Output[5], A[5], B[5]);
  not not_5 (not_5_out, Output[5]);
  and and_9 (and_9_out, not_5_out, and_5_out);
  not not_6 (not_6_out, Output[1]);
  and and_10 (and_10_out, not_6_out, and_6_out);
  and and_11 (and_11_out, A[5], and_5_out, Output[5]);
  and and_12 (and_12_out, A[1], and_6_out, Output[1]);
  or or_5 (or_5_out, and_11_out, or_3_out);
  or or_6 (or_6_out, and_12_out, or_4_out);
  xor xor_7 (Output[4], A[6], B[6]);
  not not_7 (not_7_out, Output[4]);
  xor xor_8 (Output[0], A[0], B[0]);
  not not_8 (not_8_out, Output[0]);
  and and_13 (Equal, not_8_out, and_10_out);
  and and_14 (and_14_out, not_7_out, and_9_out);
  and and_15 (and_15_out, A[6], and_9_out, Output[4]);
  or or_7 (or_7_out, and_15_out, or_5_out);
  and and_16 (and_16_out, A[0], and_10_out, Output[0]);
  or or_8 (\A__é_Maior , and_16_out, or_6_out);

  // Notes on the sheet:
  //   "A" é Maior
  //   All are equal
  //   All are equal
  //   "A" é Maior
  //   "A" é Maior
  //   All are equal
  //   All are equal
  //   "A" é Maior
  //   "A" é Maior
  //   All are equal
  //   All are equal
  //   "A" é Maior
  //   "A" é Maior
endmodule

module ALU (
  input  [7:0] A,
  input  [7:0] B,
  input  Cin,
  input  [2:0] Bit_Selector,
  output \A_é_maior ,
  output Iguais,
  output Zero,
  output [7:0] Output,
  output Cout
);

  wire _3_8__000, _3_8__001, _3_8__010, _3_8__011, _3_8__100, _3_8__101, _3_8__110, Adder_cout,
       controlled_buffer_1_out, controlled_buffer_2_out, controlled_buffer_3_out, controlled_buffer_4_out,
       LS_carry_out, RS_shift_out, subtractor_1_bout;
  wire [7:0] Adder_sum, and_1_out, Comparator_output, \LS_saída , or_1_out, \RS_saída , subtractor_1_sub;

  Comparator Comparator (.B(B), .A(A), .Output(Comparator_output), .Equal(Iguais), .\A__é_Maior (\A_é_maior ));
  assign or_1_out = A | B;  // OR_Gate or_1, 8 bits wide
  assign and_1_out = A & B;  // AND_Gate and_1, 8 bits wide
  Subtractor subtractor_1 (
    .Bin(controlled_buffer_1_out), .A(A), .B(B), .Sub(subtractor_1_sub), .Bout(subtractor_1_bout));
  assign controlled_buffer_1_out = _3_8__011 ? Cin : 1'bz;  // Controlled_Buffer controlled_buffer_1
  Left_Shifter LS (.Entrada(A), .\Saída (\LS_saída ), .Carry_out(LS_carry_out), .Carry_in(controlled_buffer_2_out));
  assign controlled_buffer_2_out = _3_8__010 ? Cin : 1'bz;  // Controlled_Buffer controlled_buffer_2
  Right_Shifter RS (.Entrada(A), .\Saída (\RS_saída ), .Shift_Out(RS_shift_out), .Shift_In(controlled_buffer_3_out));
  assign controlled_buffer_3_out = _3_8__001 ? Cin : 1'bz;  // Controlled_Buffer controlled_buffer_3
  Adder Adder (.A(A), .B(B), .Cin(controlled_buffer_4_out), .Sum(Adder_sum), .Cout(Adder_cout));
  assign controlled_buffer_4_out = _3_8__000 ? Cin : 1'bz;  // Controlled_Buffer controlled_buffer_4
  _3_to_8 _3_8 (
    .A(Bit_Selector[2]), .B(Bit_Selector[1]), .C(Bit_Selector[0]), ._000(_3_8__000), ._001(_3_8__001),
    ._010(_3_8__010), ._011(_3_8__011), ._100(_3_8__100), ._101(_3_8__101), ._110(_3_8__110));  // open: _111
  assign Output = _3_8__100 ? and_1_out : 8'bz;  // Controlled_Buffer controlled_buffer_5
  assign Output = _3_8__110 ? Comparator_output : 8'bz;  // Controlled_Buffer controlled_buffer_6
  assign Output = _3_8__101 ? or_1_out : 8'bz;  // Controlled_Buffer controlled_buffer_7
  assign Output = _3_8__011 ? subtractor_1_sub : 8'bz;  // Controlled_Buffer controlled_buffer_8
  assign Cout = _3_8__011 ? subtractor_1_bout : 1'bz;  // Controlled_Buffer controlled_buffer_9
  assign Output = _3_8__010 ? \LS_saída  : 8'bz;  // Controlled_Buffer controlled_buffer_10
  assign Cout = _3_8__010 ? LS_carry_out : 1'bz;  // Controlled_Buffer controlled_buffer_11
  assign Output = _3_8__001 ? \RS_saída  : 8'bz;  // Controlled_Buffer controlled_buffer_12
  assign Cout = _3_8__001 ? RS_shift_out : 1'bz;  // Controlled_Buffer controlled_buffer_13
  assign Output = _3_8__000 ? Adder_sum : 8'bz;  // Controlled_Buffer controlled_buffer_14
  assign Cout = _3_8__000 ? Adder_cout : 1'bz;  // Controlled_Buffer controlled_buffer_15
  or or_2 (Zero, Output[0], Output[1], Output[2], Output[3], Output[4], Output[5], Output[6], Output[7]);
endmodule

module Subtractor (
  input  Bin,
  input  [7:0] A,
  input  [7:0] B,
  output [7:0] Sub,
  output Bout
);

  wire and_1_out, and_2_out, and_3_out, and_4_out, and_5_out, and_6_out, and_7_out, and_8_out, and_9_out,
       and_10_out, and_11_out, and_12_out, and_13_out, and_14_out, and_15_out, and_16_out, not_1_out,
       not_2_out, not_3_out, not_4_out, not_5_out, not_6_out, not_7_out, not_8_out, not_9_out, not_10_out,
       not_11_out, not_12_out, not_13_out, not_14_out, not_15_out, not_16_out, or_1_out, or_2_out, or_3_out,
       or_4_out, or_5_out, or_6_out, or_7_out, xor_1_out, xor_2_out, xor_3_out, xor_4_out, xor_5_out,
       xor_6_out, xor_7_out, xor_8_out;

  xor xor_1 (xor_1_out, A[0], B[0]);
  not not_1 (not_1_out, A[0]);
  xor xor_2 (xor_2_out, A[1], B[1]);
  not not_2 (not_2_out, A[1]);
  xor xor_3 (xor_3_out, A[2], B[2]);
  not not_3 (not_3_out, A[2]);
  xor xor_4 (xor_4_out, A[3], B[3]);
  not not_4 (not_4_out, A[3]);
  xor xor_5 (xor_5_out, B[4], A[4]);
  not not_5 (not_5_out, B[4]);
  xor xor_6 (xor_6_out, A[5], B[5]);
  not not_6 (not_6_out, A[5]);
  xor xor_7 (xor_7_out, A[6], B[6]);
  not not_7 (not_7_out, A[6]);
  xor xor_8 (xor_8_out, A[7], B[7]);
  not not_8 (not_8_out, A[7]);
  not not_9 (not_9_out, xor_1_out);
  and and_1 (and_1_out, B[0], not_1_out);
  not not_10 (not_10_out, xor_2_out);
  and and_2 (and_2_out, B[1], not_2_out);
  not not_11 (not_11_out, xor_3_out);
  and and_3 (and_3_out, B[2], not_3_out);
  not not_12 (not_12_out, xor_4_out);
  and and_4 (and_4_out, B[3], not_4_out);
  and and_5 (and_5_out, A[4], not_5_out);
  and and_6 (and_6_out, B[5], not_6_out);
  and and_7 (and_7_out, B[6], not_7_out);
  and and_8 (and_8_out, B[7], not_8_out);
  and and_9 (and_9_out, not_9_out, Bin);
  and and_10 (and_10_out, not_10_out, or_1_out);
  and and_11 (and_11_out, not_11_out, or_2_out);
  and and_12 (and_12_out, not_12_out, or_3_out);
  not not_13 (not_13_out, xor_5_out);
  and and_13 (and_13_out, not_13_out, or_4_out);
  not not_14 (not_14_out, xor_6_out);
  and and_14 (and_14_out, not_14_out, or_5_out);
  not not_15 (not_15_out, xor_7_out);
  and and_15 (and_15_out, not_15_out, or_6_out);
  not not_16 (not_16_out, xor_8_out);
  and and_16 (and_16_out, not_16_out, or_7_out);
  xor xor_9 (Sub[0], Bin, xor_1_out);
  or or_1 (or_1_out, and_9_out, and_1_out);
  xor xor_10 (Sub[1], or_1_out, xor_2_out);
  or or_2 (or_2_out, and_10_out, and_2_out);
  xor xor_11 (Sub[2], or_2_out, xor_3_out);
  or or_3 (or_3_out, and_11_out, and_3_out);
  xor xor_12 (Sub[3], or_3_out, xor_4_out);
  or or_4 (or_4_out, and_12_out, and_4_out);
  xor xor_13 (Sub[4], or_4_out, xor_5_out);
  or or_5 (or_5_out, and_13_out, and_5_out);
  xor xor_14 (Sub[5], or_5_out, xor_6_out);
  or or_6 (or_6_out, and_14_out, and_6_out);
  xor xor_15 (Sub[6], or_6_out, xor_7_out);
  or or_7 (or_7_out, and_15_out, and_7_out);
  xor xor_16 (Sub[7], or_7_out, xor_8_out);
  or or_8 (Bout, and_16_out, and_8_out);
endmodule
